# Fritzing sketch schematic (saved by Fritzing 0.9.3b)
breadboards: 1

parts:
  LED1 = LED - 3mm [color="Red (633nm)" package="3 mm [THT]"]
  LED2 = LED - 3mm [color="Red (633nm)" package="3 mm [THT]"]
  LED3 = LED - 3mm [color="Red (633nm)" package="3 mm [THT]"]
  quadrant_4 = LED - 3mm [color="Red (633nm)" package="3 mm [THT]"]
  LED4 = LED - 3mm [color="Red (633nm)" package="3 mm [THT]"]
  quadrant_5 = LED - 3mm [color="Red (633nm)" package="3 mm [THT]"]
  LED5 = LED - 3mm [color="Red (633nm)" package="3 mm [THT]"]
  LED6 = LED - 3mm [color="Red (633nm)" package="3 mm [THT]"]
  quadrant_6 = LED - 3mm [color="Red (633nm)" package="3 mm [THT]"]
  LED7 = LED - 3mm [color="Red (633nm)" package="3 mm [THT]"]
  LED8 = LED - 3mm [color="Red (633nm)" package="3 mm [THT]"]
  U1 = 74HC595 SMD [package="SO16 [SMD]"]
  R1 = Resistor [tolerance=±5% resistance=220 package="0805 [SMD]"]
  R2 = Resistor [tolerance=±5% resistance=220 package="0805 [SMD]"]
  R3 = Resistor [tolerance=±5% resistance=220 package="0805 [SMD]"]
  R4 = Resistor [tolerance=±5% resistance=220 package="0805 [SMD]"]
  R5 = Resistor [tolerance=±5% resistance=220 package="0805 [SMD]"]
  R6 = Resistor [tolerance=±5% resistance=220 package="0805 [SMD]"]
  R7 = Resistor [tolerance=±5% resistance=220 package="0805 [SMD]"]
  R8 = Resistor [tolerance=±5% resistance=220 package="0805 [SMD]"]
  R9 = Resistor [tolerance=±5% resistance=220 package="0805 [SMD]"]
  R10 = Resistor [tolerance=±5% resistance=220 package="0805 [SMD]"]
  R11 = Resistor [tolerance=±5% resistance=220 package="0805 [SMD]"]
  arduino_micro = Arduino Pro Micro (Clone)
  Digital_display_(tm1637) = Grove 4 Digit Display
  VCC1 = 4 x AAA Battery Mount
  J1 = Piezo Speaker
  S2 = Pushbutton [package=THT]

nets:
  N1: LED1.cathode, R4.Pin_1
  N2: LED1.anode, arduino_micro.A0
  N3: LED2.cathode, R3.Pin_1
  N4: LED2.anode, arduino_micro.A1
  N5: LED3.cathode, R2.Pin_1
  N6: LED3.anode, arduino_micro.A2
  N7: quadrant_4.cathode, R1.Pin_1
  N8: quadrant_4.anode, arduino_micro.A3
  N9: LED4.cathode, R8.Pin_1
  N10: LED4.anode, U1.Q4
  N11: quadrant_5.cathode, R5.Pin_1
  N12: quadrant_5.anode, U1.Q7
  N13: LED5.cathode, R9.Pin_1
  N14: LED5.anode, U1.Q6
  N15: LED6.cathode, R6.Pin_1
  N16: LED6.anode, U1.Q5
  N17: quadrant_6.cathode, R7.Pin_1
  N18: quadrant_6.anode, U1.Q3
  N19: LED7.cathode, R11.Pin_1
  N20: LED7.anode, U1.Q2
  N21: LED8.cathode, R10.Pin_1
  N22: LED8.anode, U1.Q1
  GND: U1.GND, R1.Pin_0, R2.Pin_0, R3.Pin_0, R4.Pin_0, R5.Pin_0, R6.Pin_0, R7.Pin_0, R8.Pin_0, R9.Pin_0, R10.Pin_0, R11.Pin_0, arduino_micro.GND, Digital_display_(tm1637).GND, VCC1.-
  N23: U1.MR, arduino_micro.VCC, J1.pin2, S2.leg0
  N24: U1.SH_CP, arduino_micro.D2
  N25: U1.ST_CP, arduino_micro.D3
  N26: U1.DS, arduino_micro.D9
  VCC: U1.VCC, Digital_display_(tm1637).VCC
  N27: arduino_micro.D5, Digital_display_(tm1637).DIO
  N28: arduino_micro.D6, Digital_display_(tm1637).CLK
  N29: arduino_micro.D16, J1.pin1
  N30: VCC1.+, S2.leg1

notes:
  Quadrant display
  Binary display
  decimal display
  buzzer
